// Logisim project ALU.circ as structural Verilog: 19 circuits, main circuit Add/Subtract Circuit
module main (
  input  SIGN_A,
  input  A3,
  input  A2,
  input  A1,
  input  A0,
  input  sign_B,
  input  B3,
  input  B2,
  input  B1,
  input  B0,
  input  _00____ADD,
  input  _01__SUB
);

  wire bcd_7_segment_1_a_2, bcd_7_segment_1_c_2, bcd_7_segment_1_c_3, bcd_7_segment_1_d_2, bcd_7_segment_1_e,
       bcd_7_segment_1_f, bcd_7_segment_1_g, bcd_7_segment_2_a_2, bcd_7_segment_2_c_2, bcd_7_segment_2_c_3,
       bcd_7_segment_2_d_2, bcd_7_segment_2_e, bcd_7_segment_2_f, bcd_7_segment_2_g, bcd_7_segment_3_a_2,
       bcd_7_segment_3_c_2, bcd_7_segment_3_c_3, bcd_7_segment_3_d_2, bcd_7_segment_3_e, bcd_7_segment_3_f,
       bcd_7_segment_3_g, binary_to_bcd_1_h, binary_to_bcd_1_h_2, binary_to_bcd_1_t, binary_to_bcd_1_t_2,
       binary_to_bcd_1_t_3, binary_to_bcd_1_t_4, binary_to_bcd_1_u, binary_to_bcd_1_u_2, binary_to_bcd_1_u_3,
       binary_to_bcd_1_u_4, integration_1_division_by_zero, integration_1_r0, integration_1_r1,
       integration_1_r2, integration_1_r3, integration_1_r4, integration_1_r5, integration_1_r6,
       integration_1_r7, integration_1_sign_flag, integration_1_zero_flag;

  LED ZERO_REFULT (.in(integration_1_zero_flag));
  LED SIGN_FLAG (.in(integration_1_sign_flag));
  LED DIVIDE_BY_ZERO (.in(integration_1_division_by_zero));
  BCD_7_Segment bcd_7_segment_1 (
    .A(1'b0), .B(1'b0), .C(binary_to_bcd_1_h), .D(binary_to_bcd_1_h_2), .a_2(bcd_7_segment_1_a_2),
    .c_2(bcd_7_segment_1_c_2), .c_3(bcd_7_segment_1_c_3), .d_2(bcd_7_segment_1_d_2), .e(bcd_7_segment_1_e),
    .f(bcd_7_segment_1_f), .g(bcd_7_segment_1_g));
  _7_Segment_Display u_7_segment_display_1 (
    .g(bcd_7_segment_1_g), .f(bcd_7_segment_1_f), .a(bcd_7_segment_1_a_2), .b(bcd_7_segment_1_c_2),
    .e(bcd_7_segment_1_e), .d(bcd_7_segment_1_d_2), .c(bcd_7_segment_1_c_3));  // open: dp
  Integration integration_1 (
    .SIGN_FLAG(integration_1_sign_flag), .DIVISION_BY_ZERO(integration_1_division_by_zero), .S0(_01__SUB),
    .S1(_00____ADD), .ZERO_FLAG(integration_1_zero_flag), .SIGN_A(SIGN_A), .A3(A3), .A2(A2), .A1(A1),
    .A0(A0), .sign_B(sign_B), .B3(B3), .B2(B2), .B1(B1), .B0(B0), .R7(integration_1_r7),
    .R6(integration_1_r6), .R5(integration_1_r5), .R4(integration_1_r4), .R3(integration_1_r3),
    .R2(integration_1_r2), .R1(integration_1_r1), .R0(integration_1_r0));
  Binary_To_BCD binary_to_bcd_1 (
    .ZERO(1'b0), .B7(integration_1_r7), .B6(integration_1_r6), .B5(integration_1_r5), .B4(integration_1_r4),
    .B3(integration_1_r3), .B2(integration_1_r2), .B1(integration_1_r1), .B0(integration_1_r0),
    .h(binary_to_bcd_1_h), .h_2(binary_to_bcd_1_h_2), .t(binary_to_bcd_1_t), .t_2(binary_to_bcd_1_t_2),
    .t_3(binary_to_bcd_1_t_3), .t_4(binary_to_bcd_1_t_4), .u(binary_to_bcd_1_u), .u_2(binary_to_bcd_1_u_2),
    .u_3(binary_to_bcd_1_u_3), .u_4(binary_to_bcd_1_u_4));
  BCD_7_Segment bcd_7_segment_2 (
    .A(binary_to_bcd_1_t), .B(binary_to_bcd_1_t_2), .C(binary_to_bcd_1_t_3), .D(binary_to_bcd_1_t_4),
    .a_2(bcd_7_segment_2_a_2), .c_2(bcd_7_segment_2_c_2), .c_3(bcd_7_segment_2_c_3),
    .d_2(bcd_7_segment_2_d_2), .e(bcd_7_segment_2_e), .f(bcd_7_segment_2_f), .g(bcd_7_segment_2_g));
  _7_Segment_Display u_7_segment_display_2 (
    .g(bcd_7_segment_2_g), .f(bcd_7_segment_2_f), .a(bcd_7_segment_2_a_2), .b(bcd_7_segment_2_c_2),
    .e(bcd_7_segment_2_e), .d(bcd_7_segment_2_d_2), .c(bcd_7_segment_2_c_3));  // open: dp
  BCD_7_Segment bcd_7_segment_3 (
    .A(binary_to_bcd_1_u), .B(binary_to_bcd_1_u_2), .C(binary_to_bcd_1_u_3), .D(binary_to_bcd_1_u_4),
    .a_2(bcd_7_segment_3_a_2), .c_2(bcd_7_segment_3_c_2), .c_3(bcd_7_segment_3_c_3),
    .d_2(bcd_7_segment_3_d_2), .e(bcd_7_segment_3_e), .f(bcd_7_segment_3_f), .g(bcd_7_segment_3_g));
  _7_Segment_Display u_7_segment_display_3 (
    .g(bcd_7_segment_3_g), .f(bcd_7_segment_3_f), .a(bcd_7_segment_3_a_2), .b(bcd_7_segment_3_c_2),
    .e(bcd_7_segment_3_e), .d(bcd_7_segment_3_d_2), .c(bcd_7_segment_3_c_3));  // open: dp

  // Notes on the sheet:
  //   HUNDEREDS
  //   11=>DIV
  //   TENS
  //   10=>MULT
  //   UNITS
endmodule

module Add_Subtract_Circuit (
  input  A4,
  input  A3,
  input  A2,
  input  A1,
  input  A0,
  input  MODE_OF_OPERATION,
  input  B4,
  input  B3,
  input  B2,
  input  B1,
  input  B0,
  output R4,
  output R3,
  output R2,
  output R1,
  output R0,
  output SIGN
);

  wire and_1_out, and_2_out, and_3_out, and_4_out, comparator_1_out_5, full_adder_1_x, full_adder_1_y,
       full_adder_2_x, full_adder_2_y, full_adder_3_x, full_adder_3_y, full_adder_4_x, full_adder_4_y,
       half_adder_1_out_4, half_adder_2_out_4, half_adder_3_out_4, half_adder_4_out_4, not_1_out, not_2_out,
       xor_1_out, xor_2_out, xor_3_out, xor_4_out, xor_5_out, xor_6_out, xor_7_out, xor_8_out, xor_9_out,
       xor_10_out, xor_11_out, xor_12_out;

  xor xor_1 (xor_1_out, MODE_OF_OPERATION, B4);
  and and_1 (and_1_out, A4, full_adder_4_y);
  and and_2 (and_2_out, xor_1_out, not_1_out);
  or or_1 (SIGN, and_1_out, and_2_out);
  xor xor_2 (xor_2_out, xor_1_out, A4);
  not not_1 (not_1_out, full_adder_4_y);
  not not_2 (not_2_out, xor_2_out);
  and and_3 (and_3_out, not_2_out, full_adder_4_y);
  Comparator comparator_1 (
    .in_1({A3, A2, A1, A0}), .in_2({B3, B2, B1, B0}), .out_5(comparator_1_out_5));  // open: out_3, out_4
  xor xor_3 (xor_3_out, B0, xor_2_out);
  xor xor_4 (xor_4_out, B1, xor_2_out);
  xor xor_5 (xor_5_out, B2, xor_2_out);
  xor xor_6 (xor_6_out, B3, xor_2_out);
  and and_4 (and_4_out, comparator_1_out_5, xor_2_out);
  Full_Adder full_adder_1 (.a(xor_2_out), .b(A0), .c(xor_3_out), .x(full_adder_1_x), .y(full_adder_1_y));
  Full_Adder full_adder_2 (.a(full_adder_1_y), .b(A1), .c(xor_4_out), .x(full_adder_2_x), .y(full_adder_2_y));
  Full_Adder full_adder_3 (.a(full_adder_2_y), .b(A2), .c(xor_5_out), .x(full_adder_3_x), .y(full_adder_3_y));
  Full_Adder full_adder_4 (.a(full_adder_3_y), .b(A3), .c(xor_6_out), .x(full_adder_4_x), .y(full_adder_4_y));
  xor xor_7 (xor_7_out, and_3_out, and_4_out);
  xor xor_8 (xor_8_out, full_adder_1_x, and_4_out);
  xor xor_9 (xor_9_out, full_adder_2_x, and_4_out);
  xor xor_10 (xor_10_out, full_adder_3_x, and_4_out);
  xor xor_11 (xor_11_out, full_adder_4_x, and_4_out);
  xor xor_12 (xor_12_out, xor_7_out, and_4_out);
  Half_Adder half_adder_1 (.in_1(xor_8_out), .in_2(and_4_out), .out_3(R0), .out_4(half_adder_1_out_4));
  Half_Adder half_adder_2 (.in_1(xor_9_out), .in_2(half_adder_1_out_4), .out_3(R1), .out_4(half_adder_2_out_4));
  Half_Adder half_adder_3 (.in_1(xor_10_out), .in_2(half_adder_2_out_4), .out_3(R2), .out_4(half_adder_3_out_4));
  Half_Adder half_adder_4 (.in_1(xor_11_out), .in_2(half_adder_3_out_4), .out_3(R3), .out_4(half_adder_4_out_4));
  Half_Adder half_adder_5 (.in_1(xor_12_out), .in_2(half_adder_4_out_4), .out_3(R4));  // open: out_4

  // Notes on the sheet:
  //   REAL MODE
  //   A
  //   B
  //   COMPARATOR
  //   FA
  //   HA
  //   SIGN
  //   RESULT
endmodule

module Full_Adder (
  input  a,
  input  b,
  input  c,
  output x,
  output y
);

  wire and_1_out, and_2_out, and_3_out, and_4_out, and_5_out, and_6_out, and_7_out, not_1_out, not_2_out,
       not_3_out, not_4_out, not_5_out, not_6_out;

  not not_1 (not_1_out, a);
  not not_2 (not_2_out, b);
  not not_3 (not_3_out, a);
  not not_4 (not_4_out, c);
  not not_5 (not_5_out, b);
  not not_6 (not_6_out, c);
  and and_1 (and_1_out, b, c);
  and and_2 (and_2_out, a, c);
  and and_3 (and_3_out, a, b);
  and and_4 (and_4_out, not_1_out, not_2_out, c);
  and and_5 (and_5_out, not_3_out, b, not_4_out);
  and and_6 (and_6_out, a, not_5_out, not_6_out);
  and and_7 (and_7_out, a, b, c);
  or or_1 (y, and_1_out, and_2_out, and_3_out);
  or or_2 (x, and_4_out, and_5_out, and_6_out, and_7_out);
endmodule

module Half_Adder (
  input  in_1,
  input  in_2,
  output out_3,
  output out_4
);

  xor xor_1 (out_3, in_1, in_2);
  and and_1 (out_4, in_1, in_2);
endmodule

module Divider_Circuit (
  input  B4,
  input  B3,
  input  B2,
  input  B1,
  input  B0,
  input  A4,
  input  A3,
  input  A2,
  input  A1,
  input  A0,
  output DIVIDE_BY_ZERO,
  output NEGATIVE_FLAG,
  output Q3,
  output Q2,
  output Q1,
  output Q2_2
);

  wire COMPARATOR_2_out_3, COMPARATOR_2_out_4, COMPARATOR_3_out_3, COMPARATOR_3_out_4, COMPARATOR_4_out_3,
       COMPARATOR_4_out_4, COMPARATOR_out_3, COMPARATOR_out_4, or_5_out, or_6_out;
  wire [3:0] ADD_2_out_4, ADD_3_out_4, ADD_out_4, MULTIPLIER_2_out_6, MULTIPLIER_3_out_6, MULTIPLIER_out_6,
       SHIFTER_2_out_5, SHIFTER_3_out_5, SHIFTER_out_5, SUB_2_out_4, SUB_3_out_4, SUB_out_4;

  Comparator COMPARATOR (
    .in_1({3'b000, A3}), .in_2({B3, B2, B1, B0}), .out_3(COMPARATOR_out_3), .out_4(COMPARATOR_out_4));  // open: out_5
  Comparator COMPARATOR_2 (
    .in_1(ADD_out_4), .in_2({B3, B2, B1, B0}), .out_3(COMPARATOR_2_out_3), .out_4(COMPARATOR_2_out_4));  // open: out_5
  Comparator COMPARATOR_3 (
    .in_1(ADD_2_out_4), .in_2({B3, B2, B1, B0}), .out_3(COMPARATOR_3_out_3), .out_4(COMPARATOR_3_out_4));  // open: out_5
  Comparator COMPARATOR_4 (
    .in_1(ADD_3_out_4), .in_2({B3, B2, B1, B0}), .out_3(COMPARATOR_4_out_3), .out_4(COMPARATOR_4_out_4));  // open: out_5
  or or_1 (Q3, COMPARATOR_out_3, COMPARATOR_out_4);
  or or_2 (Q2, COMPARATOR_2_out_3, COMPARATOR_2_out_4);
  or or_3 (Q1, COMPARATOR_3_out_3, COMPARATOR_3_out_4);
  or or_4 (Q2_2, COMPARATOR_4_out_3, COMPARATOR_4_out_4);
  or or_5 (or_5_out, B0, B1);
  or or_6 (or_6_out, or_5_out, B2);
  xor xor_1 (NEGATIVE_FLAG, A4, B4);
  _4x1_multiplier MULTIPLIER (
    .A0(B0), .A1(B1), .A2(B2), .A3(B3), .B(Q3), .out_6(MULTIPLIER_out_6[0]), .out_7(MULTIPLIER_out_6[1]),
    .out_8(MULTIPLIER_out_6[2]), .out_9(MULTIPLIER_out_6[3]));
  _4x1_multiplier MULTIPLIER_2 (
    .A0(B0), .A1(B1), .A2(B2), .A3(B3), .B(Q2), .out_6(MULTIPLIER_2_out_6[0]), .out_7(MULTIPLIER_2_out_6[1]),
    .out_8(MULTIPLIER_2_out_6[2]), .out_9(MULTIPLIER_2_out_6[3]));
  _4x1_multiplier MULTIPLIER_3 (
    .A0(B0), .A1(B1), .A2(B2), .A3(B3), .B(Q1), .out_6(MULTIPLIER_3_out_6[0]), .out_7(MULTIPLIER_3_out_6[1]),
    .out_8(MULTIPLIER_3_out_6[2]), .out_9(MULTIPLIER_3_out_6[3]));
  nor nor_1 (DIVIDE_BY_ZERO, or_6_out, B3);
  Unsigned_Adder_Subtractor SUB (.out_4(SUB_out_4), .in_3(1'b1), .B(MULTIPLIER_out_6), .A({3'b000, A3}));
  Unsigned_Adder_Subtractor SUB_2 (.out_4(SUB_2_out_4), .in_3(1'b1), .B(MULTIPLIER_2_out_6), .A(ADD_out_4));
  Shifter SHIFTER (
    .in_1(SUB_out_4[0]), .in_2(SUB_out_4[1]), .in_3(SUB_out_4[2]), .in_4(SUB_out_4[3]),
    .out_5(SHIFTER_out_5[0]), .out_6(SHIFTER_out_5[1]), .out_7(SHIFTER_out_5[2]), .out_8(SHIFTER_out_5[3]));
  Shifter SHIFTER_2 (
    .in_1(SUB_2_out_4[0]), .in_2(SUB_2_out_4[1]), .in_3(SUB_2_out_4[2]), .in_4(SUB_2_out_4[3]),
    .out_5(SHIFTER_2_out_5[0]), .out_6(SHIFTER_2_out_5[1]), .out_7(SHIFTER_2_out_5[2]),
    .out_8(SHIFTER_2_out_5[3]));
  Unsigned_Adder_Subtractor SUB_3 (.out_4(SUB_3_out_4), .in_3(1'b1), .B(MULTIPLIER_3_out_6), .A(ADD_2_out_4));
  Unsigned_Adder_Subtractor ADD (.out_4(ADD_out_4), .in_3(1'b0), .B({3'b000, A2}), .A(SHIFTER_out_5));
  Unsigned_Adder_Subtractor ADD_2 (.out_4(ADD_2_out_4), .in_3(1'b0), .B({3'b000, A1}), .A(SHIFTER_2_out_5));
  Shifter SHIFTER_3 (
    .in_1(SUB_3_out_4[0]), .in_2(SUB_3_out_4[1]), .in_3(SUB_3_out_4[2]), .in_4(SUB_3_out_4[3]),
    .out_5(SHIFTER_3_out_5[0]), .out_6(SHIFTER_3_out_5[1]), .out_7(SHIFTER_3_out_5[2]),
    .out_8(SHIFTER_3_out_5[3]));
  Unsigned_Adder_Subtractor ADD_3 (.out_4(ADD_3_out_4), .in_3(1'b0), .B({3'b000, A0}), .A(SHIFTER_3_out_5));

  // Notes on the sheet:
  //   DIVISOR
  //   DIVIDEND
endmodule

module _4x1_multiplier (
  input  A0,
  input  A1,
  input  A2,
  input  A3,
  input  B,
  output out_6,
  output out_7,
  output out_8,
  output out_9
);

  and and_1 (out_6, A0, B);
  and and_2 (out_7, A1, B);
  and and_3 (out_8, A2, B);
  and and_4 (out_9, A3, B);
endmodule

module Multiplier_Circuit (
  input  a4,
  input  a3,
  input  a2,
  input  a1,
  input  a0,
  input  B0,
  input  B1,
  input  B2,
  input  B3,
  input  in_10,
  output out_11,
  output out_12,
  output out_13,
  output out_14,
  output out_15,
  output out_16,
  output out_17,
  output out_18,
  output out_19
);

  wire and_1_out, and_2_out, and_3_out, and_4_out, and_5_out, and_6_out, and_7_out, and_8_out, and_9_out,
       and_10_out, and_11_out, and_12_out, and_13_out, and_14_out, and_15_out, multiplier_fa_2_cout,
       multiplier_fa_2_r, multiplier_fa_3_cout, multiplier_fa_4_cout, multiplier_fa_5_cout,
       multiplier_fa_5_r, multiplier_fa_6_cout, multiplier_fa_6_r, multiplier_fa_7_cout, multiplier_fa_7_r,
       multiplier_fa_8_cout, multiplier_fa_8_r, multiplier_ha_1_c, multiplier_ha_1_out_3, multiplier_ha_2_c,
       multiplier_ha_3_c, multiplier_ha_4_c;

  xor xor_1 (out_11, a4, in_10);
  and and_1 (and_1_out, B3, a3);
  Multiplier_FA multiplier_fa_1 (
    .A(multiplier_fa_3_cout), .B(and_1_out), .Cin(multiplier_fa_2_cout), .R(out_13), .Cout(out_12));
  and and_2 (and_2_out, a3, B2);
  Multiplier_FA multiplier_fa_2 (
    .A(multiplier_fa_5_cout), .B(and_2_out), .Cin(multiplier_ha_1_c), .R(multiplier_fa_2_r),
    .Cout(multiplier_fa_2_cout));
  and and_3 (and_3_out, B3, a2);
  Multiplier_FA multiplier_fa_3 (
    .A(multiplier_fa_4_cout), .B(and_3_out), .Cin(multiplier_fa_2_r), .R(out_14), .Cout(multiplier_fa_3_cout));
  and and_4 (and_4_out, B1, a3);
  Multiplier_HA multiplier_ha_1 (
    .A(multiplier_fa_6_cout), .B(and_4_out), .out_3(multiplier_ha_1_out_3), .C(multiplier_ha_1_c));
  and and_5 (and_5_out, B3, a1);
  Multiplier_FA multiplier_fa_4 (
    .A(multiplier_ha_2_c), .B(multiplier_fa_5_r), .Cin(and_5_out), .R(out_15), .Cout(multiplier_fa_4_cout));
  and and_6 (and_6_out, a2, B2);
  Multiplier_FA multiplier_fa_5 (
    .A(multiplier_fa_7_cout), .B(multiplier_ha_1_out_3), .Cin(and_6_out), .R(multiplier_fa_5_r),
    .Cout(multiplier_fa_5_cout));
  and and_7 (and_7_out, a3, B0);
  and and_8 (and_8_out, B1, a2);
  Multiplier_FA multiplier_fa_6 (
    .A(multiplier_fa_8_cout), .B(and_7_out), .Cin(and_8_out), .R(multiplier_fa_6_r),
    .Cout(multiplier_fa_6_cout));
  and and_9 (and_9_out, a1, B2);
  Multiplier_FA multiplier_fa_7 (
    .A(multiplier_ha_3_c), .B(and_9_out), .Cin(multiplier_fa_6_r), .R(multiplier_fa_7_r),
    .Cout(multiplier_fa_7_cout));
  and and_10 (and_10_out, B3, a0);
  Multiplier_HA multiplier_ha_2 (.A(multiplier_fa_7_r), .B(and_10_out), .out_3(out_16), .C(multiplier_ha_2_c));
  and and_11 (and_11_out, B1, a1);
  and and_12 (and_12_out, a2, B0);
  Multiplier_FA multiplier_fa_8 (
    .A(multiplier_ha_4_c), .B(and_12_out), .Cin(and_11_out), .R(multiplier_fa_8_r),
    .Cout(multiplier_fa_8_cout));
  and and_13 (and_13_out, a0, B2);
  Multiplier_HA multiplier_ha_3 (.A(and_13_out), .B(multiplier_fa_8_r), .out_3(out_17), .C(multiplier_ha_3_c));
  and and_14 (and_14_out, a1, B0);
  and and_15 (and_15_out, B1, a0);
  Multiplier_HA multiplier_ha_4 (.A(and_14_out), .B(and_15_out), .out_3(out_18), .C(multiplier_ha_4_c));
  and and_16 (out_19, a0, B0);

  // Notes on the sheet:
  //   R8
  //   R7
  //   R6
  //   R5
  //   R4
  //   R3
  //   R2
  //   R1
  //   R0
endmodule

module Multiplier_FA (
  input  A,
  input  B,
  input  Cin,
  output R,
  output Cout
);

  wire and_1_out, and_2_out, xor_1_out;

  and and_1 (and_1_out, A, B);
  xor xor_1 (xor_1_out, A, B);
  xor xor_2 (R, xor_1_out, Cin);
  and and_2 (and_2_out, Cin, xor_1_out);
  or or_1 (Cout, and_2_out, and_1_out);
endmodule

module Multiplier_HA (
  input  A,
  input  B,
  output out_3,
  output C
);

  xor xor_1 (out_3, A, B);
  and and_1 (C, B, A);

  // Notes on the sheet:
  //   R
endmodule

module Multiplication (
  input  in_1,
  input  A,
  input  in_3,
  input  in_4,
  input  in_5,
  input  in_6,
  input  in_7,
  input  in_8,
  input  B,
  input  in_10,
  output Negative_Flag,
  output out_12,
  output out_13,
  output out_14,
  output out_15,
  output out_16,
  output out_17,
  output AxB,
  output out_19
);

  Multiplier_Circuit multiplier_circuit_1 (
    .out_11(Negative_Flag), .out_12(out_12), .out_13(out_13), .out_14(out_14), .out_15(out_15),
    .out_16(out_16), .out_17(out_17), .out_18(AxB), .out_19(out_19), .a4(in_1), .a3(A), .a2(in_3), .a1(in_4),
    .a0(in_5), .B0(in_10), .B1(B), .B2(in_8), .B3(in_7), .in_10(in_6));
endmodule

module Divison (
  input  B4,
  input  B3,
  input  B2,
  input  B1,
  input  B0,
  input  A4,
  input  A3,
  input  A2,
  input  A1,
  input  A0,
  output NEGARIVE_FLAG,
  output DIVIDE_BY_ZERO,
  output R3,
  output R2,
  output R1,
  output R0
);

  Divider_Circuit divider_circuit_1 (
    .B4(B4), .B3(B3), .B2(B2), .B1(B1), .B0(B0), .A4(A4), .A3(A3), .A2(A2), .A1(A1), .A0(A0),
    .DIVIDE_BY_ZERO(DIVIDE_BY_ZERO), .NEGATIVE_FLAG(NEGARIVE_FLAG), .Q3(R3), .Q2(R2), .Q1(R1), .Q2_2(R0));

  // Notes on the sheet:
  //   B
  //   A
  //   A÷B
endmodule

module Binary_To_BCD (
  input  ZERO,
  input  B7,
  input  B6,
  input  B5,
  input  B4,
  input  B3,
  input  B2,
  input  B1,
  input  B0,
  output h,
  output h_2,
  output t,
  output t_2,
  output t_3,
  output t_4,
  output u,
  output u_2,
  output u_3,
  output u_4
);

  wire n4_bit_binary_conv_1_s0, n4_bit_binary_conv_1_s1, n4_bit_binary_conv_1_s2, n4_bit_binary_conv_3_s0,
       n4_bit_binary_conv_3_s1, n4_bit_binary_conv_3_s2, n4_bit_binary_conv_3_s3, n4_bit_binary_conv_4_s0,
       n4_bit_binary_conv_4_s1, n4_bit_binary_conv_4_s2, n4_bit_binary_conv_4_s3, n4_bit_binary_conv_5_s0,
       n4_bit_binary_conv_5_s1, n4_bit_binary_conv_5_s2, n4_bit_binary_conv_5_s3, n4_bit_binary_conv_6_s0,
       n4_bit_binary_conv_6_s1, n4_bit_binary_conv_6_s2, n4_bit_binary_conv_6_s3;

  _4_Bit_Binary_Conv u_4_bit_binary_conv_1 (
    .S3(h), .S2(n4_bit_binary_conv_1_s2), .S1(n4_bit_binary_conv_1_s1), .S0(n4_bit_binary_conv_1_s0),
    .A3(ZERO), .A2(n4_bit_binary_conv_4_s3), .A1(n4_bit_binary_conv_5_s3), .A0(n4_bit_binary_conv_6_s3));
  _4_Bit_Binary_Conv u_4_bit_binary_conv_2 (
    .S3(h_2), .S2(t), .S1(t_2), .S0(t_3), .A3(n4_bit_binary_conv_1_s2), .A2(n4_bit_binary_conv_1_s1),
    .A1(n4_bit_binary_conv_1_s0), .A0(n4_bit_binary_conv_3_s3));
  _4_Bit_Binary_Conv u_4_bit_binary_conv_3 (
    .S3(n4_bit_binary_conv_3_s3), .S2(n4_bit_binary_conv_3_s2), .S1(n4_bit_binary_conv_3_s1),
    .S0(n4_bit_binary_conv_3_s0), .A3(n4_bit_binary_conv_6_s2), .A2(n4_bit_binary_conv_6_s1),
    .A1(n4_bit_binary_conv_6_s0), .A0(B2));
  _4_Bit_Binary_Conv u_4_bit_binary_conv_4 (
    .S3(n4_bit_binary_conv_4_s3), .S2(n4_bit_binary_conv_4_s2), .S1(n4_bit_binary_conv_4_s1),
    .S0(n4_bit_binary_conv_4_s0), .A3(ZERO), .A2(B7), .A1(B6), .A0(B5));
  _4_Bit_Binary_Conv u_4_bit_binary_conv_5 (
    .S3(n4_bit_binary_conv_5_s3), .S2(n4_bit_binary_conv_5_s2), .S1(n4_bit_binary_conv_5_s1),
    .S0(n4_bit_binary_conv_5_s0), .A3(n4_bit_binary_conv_4_s2), .A2(n4_bit_binary_conv_4_s1),
    .A1(n4_bit_binary_conv_4_s0), .A0(B4));
  _4_Bit_Binary_Conv u_4_bit_binary_conv_6 (
    .S3(n4_bit_binary_conv_6_s3), .S2(n4_bit_binary_conv_6_s2), .S1(n4_bit_binary_conv_6_s1),
    .S0(n4_bit_binary_conv_6_s0), .A3(n4_bit_binary_conv_5_s2), .A2(n4_bit_binary_conv_5_s1),
    .A1(n4_bit_binary_conv_5_s0), .A0(B3));
  _4_Bit_Binary_Conv u_4_bit_binary_conv_7 (
    .S3(t_4), .S2(u), .S1(u_2), .S0(u_3), .A3(n4_bit_binary_conv_3_s2), .A2(n4_bit_binary_conv_3_s1),
    .A1(n4_bit_binary_conv_3_s0), .A0(B1));

  assign u_4 = B0;

  // Notes on the sheet:
  //   c7
  //   c4
  //   c1
  //   c2
  //   c3
  //   c5
endmodule

module Adding_and_Subtracting (
  input  in_1,
  input  in_2,
  input  A,
  input  in_4,
  input  in_5,
  input  B,
  input  in_7,
  input  in_8,
  input  in_9,
  input  in_10,
  input  MODE,
  output out_12,
  output out_13,
  output R,
  output out_15,
  output out_16,
  output out_17
);

  Add_Subtract_Circuit add_subtract_circuit_1 (
    .MODE_OF_OPERATION(MODE), .B4(in_1), .B3(in_2), .B2(A), .B1(in_4), .B0(in_5), .A4(B), .A3(in_7),
    .A2(in_8), .A1(in_9), .A0(in_10), .R4(out_13), .R3(R), .R2(out_15), .R1(out_16), .R0(out_17),
    .SIGN(out_12));

  // Notes on the sheet:
  //   0 FOR ADDITION
  //   1 FOR SUBTRACTION
endmodule

module Integration (
  input  SIGN_A,
  input  A3,
  input  A2,
  input  A1,
  input  A0,
  input  sign_B,
  input  B3,
  input  B2,
  input  B1,
  input  B0,
  input  S0,
  input  S1,
  output SIGN_FLAG,
  output DIVISION_BY_ZERO,
  output ZERO_FLAG,
  output R7,
  output R6,
  output R5,
  output R4,
  output R3,
  output R2,
  output R1,
  output R0
);

  wire ADD___SUBT_out_12, DIVISION_negarive_flag, or_1_out, or_2_out, or_3_out, or_4_out, or_5_out, or_6_out;
  wire [3:0] DIVISION_r0;
  wire [4:0] ADD___SUBT_out_17;
  wire [7:0] MULTIPLICATION_out_19;

  Multiplexer #(.select(2)) multiplexer_1 (
    .in0(ADD___SUBT_out_12), .in1(ADD___SUBT_out_12), .in2(DIVISION_negarive_flag),
    .in3(DIVISION_negarive_flag), .out(SIGN_FLAG), .sel({S1, S0}));  // open: en
  or or_1 (or_1_out, or_2_out, R6);
  nor nor_1 (ZERO_FLAG, or_1_out, R7);
  or or_2 (or_2_out, or_4_out, R5);
  Adding_and_Subtracting ADD___SUBT (
    .B(SIGN_A), .in_7(A3), .in_8(A2), .in_9(A1), .in_10(A0), .in_1(sign_B), .in_2(B3), .A(B2), .in_4(B1),
    .in_5(B0), .out_12(ADD___SUBT_out_12), .out_13(ADD___SUBT_out_17[4]), .R(ADD___SUBT_out_17[3]),
    .out_15(ADD___SUBT_out_17[2]), .out_16(ADD___SUBT_out_17[1]), .out_17(ADD___SUBT_out_17[0]), .MODE(S0));
  or or_3 (or_3_out, or_5_out, R3);
  or or_4 (or_4_out, or_3_out, R4);
  or or_5 (or_5_out, or_6_out, R2);
  or or_6 (or_6_out, R0, R1);
  Multiplication MULTIPLICATION (
    .in_1(SIGN_A), .A(A3), .in_3(A2), .in_4(A1), .in_5(A0), .out_12(MULTIPLICATION_out_19[7]),
    .out_13(MULTIPLICATION_out_19[6]), .out_14(MULTIPLICATION_out_19[5]), .out_15(MULTIPLICATION_out_19[4]),
    .out_16(MULTIPLICATION_out_19[3]), .out_17(MULTIPLICATION_out_19[2]), .AxB(MULTIPLICATION_out_19[1]),
    .out_19(MULTIPLICATION_out_19[0]), .in_6(sign_B), .in_7(B3), .in_8(B2), .B(B1), .in_10(B0));  // open: Negative_Flag
  Multiplexer #(.select(2), .width(8)) multiplexer_2 (
    .in0({3'b000, ADD___SUBT_out_17}), .in1({3'b000, ADD___SUBT_out_17}), .in2(MULTIPLICATION_out_19),
    .in3({4'b0000, DIVISION_r0}), .out({R7, R6, R5, R4, R3, R2, R1, R0}), .sel({S1, S0}));  // open: en
  Divison DIVISION (
    .B4(sign_B), .B3(B3), .B2(B2), .B1(B1), .B0(B0), .A4(SIGN_A), .A3(A3), .A2(A2), .A1(A1), .A0(A0),
    .DIVIDE_BY_ZERO(DIVISION_BY_ZERO), .NEGARIVE_FLAG(DIVISION_negarive_flag), .R3(DIVISION_r0[3]),
    .R2(DIVISION_r0[2]), .R1(DIVISION_r0[1]), .R0(DIVISION_r0[0]));
endmodule

module Shifter (
  input  in_1,
  input  in_2,
  input  in_3,
  input  in_4,
  output out_5,
  output out_6,
  output out_7,
  output out_8
);


  assign out_5 = 1'b0;
  assign out_6 = in_1;
  assign out_7 = in_2;
  assign out_8 = in_3;
endmodule

module Comparator (
  input  [3:0] in_1,
  input  [3:0] in_2,
  output out_3,
  output out_4,
  output out_5
);

  wire and_1_out, and_2_out, and_3_out, and_4_out, and_5_out, and_6_out, and_7_out, and_8_out, not_1_out,
       not_2_out, not_3_out, not_4_out, not_5_out, not_6_out, not_7_out, not_8_out, xnor_1_out, xnor_2_out,
       xnor_3_out, xnor_4_out;

  not not_1 (not_1_out, in_2[3]);
  not not_2 (not_2_out, in_2[2]);
  not not_3 (not_3_out, in_2[1]);
  xnor xnor_1 (xnor_1_out, in_1[3], in_2[3]);
  xnor xnor_2 (xnor_2_out, in_1[2], in_2[2]);
  xnor xnor_3 (xnor_3_out, in_1[1], in_2[1]);
  xnor xnor_4 (xnor_4_out, in_1[0], in_2[0]);
  not not_4 (not_4_out, in_1[3]);
  not not_5 (not_5_out, in_1[2]);
  not not_6 (not_6_out, in_1[1]);
  not not_7 (not_7_out, in_1[0]);
  and and_1 (and_1_out, in_1[3], not_1_out);
  not not_8 (not_8_out, in_2[0]);
  and and_2 (and_2_out, in_1[2], not_2_out, xnor_1_out);
  and and_3 (and_3_out, in_1[1], not_3_out, xnor_1_out, xnor_2_out);
  and and_4 (and_4_out, in_1[0], not_8_out, xnor_1_out, xnor_2_out, xnor_3_out);
  and and_5 (and_5_out, not_4_out, in_2[3]);
  and and_6 (and_6_out, not_5_out, in_2[2], xnor_1_out);
  and and_7 (and_7_out, xnor_1_out, xnor_2_out, not_6_out, in_2[1]);
  and and_8 (and_8_out, xnor_1_out, xnor_3_out, xnor_2_out, not_7_out, in_2[0]);
  or A_B (out_3, and_1_out, and_2_out, and_3_out, and_4_out);
  and A_B_2 (out_4, xnor_1_out, xnor_2_out, xnor_3_out, xnor_4_out);
  or A_B_3 (out_5, and_5_out, and_6_out, and_7_out, and_8_out);
endmodule

module BCD_7_Segment (
  input  A,
  input  B,
  input  C,
  input  D,
  output a_2,
  output c_2,
  output c_3,
  output d_2,
  output e,
  output f,
  output g
);

  wire B_C_out, B_D_out, BC_D_out, BC_out, BD_2_out, BD_out, C_D_out, CD_2_out, CD_out, not_1_out, not_2_out,
       not_3_out, or_1_out, or_2_out, or_3_out, or_4_out, or_5_out, or_9_out, or_10_out, or_11_out,
       or_12_out, or_13_out, or_14_out;

  not not_1 (not_1_out, B);
  not not_2 (not_2_out, C);
  not not_3 (not_3_out, D);
  and BD (BD_out, B, D);
  and B_D (B_D_out, not_3_out, not_1_out);
  and CD (CD_out, D, C);
  and C_D (C_D_out, not_3_out, not_2_out);
  and CD_2 (CD_2_out, C, not_3_out);
  and B_C (B_C_out, not_1_out, C);
  and BC (BC_out, B, not_2_out);
  and BD_2 (BD_2_out, B, not_3_out);
  or or_1 (or_1_out, BD_out, B_D_out);
  or or_2 (or_2_out, CD_out, not_1_out);
  or or_3 (or_3_out, B, not_2_out);
  or or_4 (or_4_out, A, B_D_out);
  and BC_D (BC_D_out, D, BC_out);
  or or_5 (or_5_out, or_1_out, A);
  or or_6 (a_2, or_5_out, C);
  or or_7 (c_2, or_2_out, C_D_out);
  or or_8 (c_3, or_3_out, D);
  or or_9 (or_9_out, or_4_out, CD_2_out);
  or or_10 (or_10_out, or_9_out, B_C_out);
  or or_11 (or_11_out, C_D_out, BD_2_out);
  or or_12 (or_12_out, or_11_out, BC_D_out);
  or or_13 (or_13_out, CD_2_out, BC_out);
  or or_14 (or_14_out, or_13_out, A);
  or or_15 (d_2, or_10_out, BC_D_out);
  or or_16 (e, B_D_out, CD_2_out);
  or or_17 (f, or_12_out, A);
  or or_18 (g, or_14_out, B_C_out);
endmodule

module Unsigned_Adder_Subtractor (
  input  [3:0] A,
  input  [3:0] B,
  input  in_3,
  output [3:0] out_4
);

  wire multiplier_fa_2_cout, multiplier_fa_3_cout, multiplier_fa_4_cout, xor_1_out, xor_2_out, xor_3_out,
       xor_4_out;

  xor xor_1 (xor_1_out, B[3], in_3);
  Multiplier_FA multiplier_fa_1 (.A(A[3]), .B(xor_1_out), .Cin(multiplier_fa_3_cout), .R(out_4[3]));  // open: Cout
  xor xor_2 (xor_2_out, B[2], in_3);
  xor xor_3 (xor_3_out, B[1], in_3);
  Multiplier_FA multiplier_fa_2 (
    .A(A[1]), .B(xor_3_out), .Cin(multiplier_fa_4_cout), .R(out_4[1]), .Cout(multiplier_fa_2_cout));
  Multiplier_FA multiplier_fa_3 (
    .A(A[2]), .B(xor_2_out), .Cin(multiplier_fa_2_cout), .R(out_4[2]), .Cout(multiplier_fa_3_cout));
  xor xor_4 (xor_4_out, B[0], in_3);
  Multiplier_FA multiplier_fa_4 (.A(A[0]), .B(xor_4_out), .Cin(in_3), .R(out_4[0]), .Cout(multiplier_fa_4_cout));
endmodule

module _4_Bit_Binary_Conv (
  input  A3,
  input  A2,
  input  A1,
  input  A0,
  output S3,
  output S2,
  output S1,
  output S0
);

  wire and_1_out, and_2_out, and_3_out, and_4_out, and_5_out, and_6_out, and_7_out, and_8_out, and_9_out,
       and_10_out, and_11_out, and_12_out, and_13_out, and_14_out, and_15_out, and_16_out, and_17_out,
       and_18_out, and_19_out, and_20_out, and_21_out, and_22_out, and_23_out, not_1_out, not_2_out,
       not_3_out, not_4_out, or_1_out, or_2_out, or_4_out;

  not not_1 (not_1_out, A3);
  not not_2 (not_2_out, A2);
  not not_3 (not_3_out, A1);
  not not_4 (not_4_out, A0);
  and and_1 (and_1_out, not_3_out, A3);
  and and_2 (and_2_out, A0, not_1_out);
  and and_3 (and_3_out, A1, not_1_out);
  and and_4 (and_4_out, not_1_out, A2);
  and and_5 (and_5_out, not_3_out, not_4_out);
  and and_6 (and_6_out, not_2_out, A3);
  and and_7 (and_7_out, not_1_out, A1);
  or or_1 (or_1_out, not_2_out, A0);
  and and_8 (and_8_out, A0, not_2_out);
  and and_9 (and_9_out, A3, not_4_out);
  and and_10 (and_10_out, A1, A2);
  and and_11 (and_11_out, and_1_out, not_2_out);
  and and_12 (and_12_out, and_3_out, A2);
  and and_13 (and_13_out, not_3_out, not_4_out);
  and and_14 (and_14_out, and_5_out, and_6_out);
  and and_15 (and_15_out, and_7_out, or_1_out);
  and and_16 (and_16_out, and_8_out, not_1_out);
  and and_17 (and_17_out, and_9_out, not_3_out);
  and and_18 (and_18_out, and_10_out, not_4_out);
  and and_19 (and_19_out, and_2_out, A2);
  or or_2 (or_2_out, and_11_out, and_19_out);
  and and_20 (and_20_out, A0, not_3_out);
  and and_21 (and_21_out, A3, not_2_out);
  or or_3 (S1, and_14_out, and_15_out);
  or or_4 (or_4_out, and_16_out, and_17_out);
  or or_5 (S3, or_2_out, and_12_out);
  and and_22 (and_22_out, and_4_out, and_13_out);
  and and_23 (and_23_out, and_20_out, and_21_out);
  or or_6 (S0, or_4_out, and_18_out);
  or or_7 (S2, and_22_out, and_23_out);

  // Notes on the sheet:
  //   A2
  //   A1
  //   A0
  //   s3
endmodule
